# Fritzing sketch corizo major (saved by Fritzing 0.9.3b)
breadboards: 3

parts:
  Part1 = Arduino Mega 2560 (Rev3)
  Part2 = InvenSense MPU6050
  M1 = Getriebemotor
  M2 = Getriebemotor
  M3 = Getriebemotor
  M4 = Getriebemotor
  VCC1 = 4 x AAA Battery Mount  # not connected
  IC1 = L293D [package=THT]
  IC2 = L293D [package=THT]

nets:
  N1: Part1.D21/SCL, Part2.SCL
  N2: Part1.D20/SDA, Part2.SDA
  N3: Part1.D13_PWM, IC2.Enable_1
  N4: Part1.D12_PWM, IC2.In_4
  N5: Part1.D11_PWM, IC2.In_3
  N6: Part1.D10_PWM, IC2.In_2
  N7: Part1.D9_PWM, IC2.In_1
  N8: Part1.D8_PWM, IC2.Enable_2
  5V: Part1.5V, Part2.VCC
  GND: Part1.GND, Part2.GND, IC1.0V, IC2.0V
  N9: Part1.D2_PWM, IC1.Enable_2
  N10: Part1.D3_PWM, IC1.In_3
  N11: Part1.D4_PWM, IC1.In_4
  N12: Part1.D5_PWM, IC1.In_2
  N13: Part1.D6_PWM, IC1.In_1
  N14: Part1.D7_PWM, IC1.Enable_1
  N15: M1.pin_1, IC2.Out_4_(_Controlled_by_Enable_2_)
  N16: M1.pin_2, IC2.Out_3_(_Controlled_by_Enable_2_)
  N17: M2.pin_1, IC1.Out_4_(_Controlled_by_Enable_2_)
  N18: M2.pin_2, IC1.Out_3_(_Controlled_by_Enable_2_)
  N19: M3.pin_1, IC1.Out_2_(_Controlled_by_Enable_1_)
  N20: M3.pin_2, IC1.Out_1_(_Controlled_by_Enable_1_)
  N21: M4.pin_1, IC2.Out_2_(_Controlled_by_Enable_1_)
  N22: M4.pin_2, IC2.Out_1_(_Controlled_by_Enable_1_)
  N23: IC1.+V, IC2.+V

// code stored in the sketch: final.ino
#include <Adafruit_MPU6050.h>
#include <Adafruit_Sensor.h>
#include <Wire.h>


#define IN1_1 13 // Enable pin for motor 1 (left wheel 1)
#define IN2_1 12 // Direction pin 1 for motor 1
#define IN3_1 11 // Direction pin 2 for motor 1
#define IN1_2 8 // Enable pin for motor 2 (left wheel 2)
#define IN2_2 10 // Direction pin 1 for motor 2
#define IN3_2 9 // Direction pin 2 for motor 2


#define IN1_3 7  // Enable pin for motor 3 (right wheel 1)
#define IN2_3 6 // Direction pin 1 for motor 3
#define IN3_3 5 // Direction pin 2 for motor 3
#define IN1_4 2 // Enable pin for motor 4 (right wheel 2)
#define IN2_4 4   // Direction pin 1 for motor 4
#define IN3_4 3  // Direction pin 2 for motor 4


Adafruit_MPU6050 mpu;


int motorSpeed = 240; 


void setup() {
  pinMode(IN1_1, OUTPUT);
  pinMode(IN2_1, OUTPUT);
  pinMode(IN3_1, OUTPUT);
  pinMode(IN1_2, OUTPUT);
  pinMode(IN2_2, OUTPUT);
  pinMode(IN3_2, OUTPUT);


  pinMode(IN1_3, OUTPUT);
  pinMode(IN2_3, OUTPUT);
  pinMode(IN3_3, OUTPUT);
  pinMode(IN1_4, OUTPUT);
  pinMode(IN2_4, OUTPUT);
  pinMode(IN3_4, OUTPUT);


  Serial.begin(115200);
  while (!Serial)
    delay(10); 


  Serial.println("Adafruit MPU6050 test!");


  if (!mpu.begin()) {
    Serial.println("Failed to find MPU6050 chip");
    while (1) {
      delay(10);
    }
  }
  Serial.println("MPU6050 Found!");


  mpu.setAccelerometerRange(MPU6050_RANGE_8_G);
  Serial.print("Accelerometer range set to: ");
  switch (mpu.getAccelerometerRange()) {
  case MPU6050_RANGE_2_G:
    Serial.println("+-2G");
    break;
  case MPU6050_RANGE_4_G:
    Serial.println("+-4G");
    break;
  case MPU6050_RANGE_8_G:
    Serial.println("+-8G");
    break;
  case MPU6050_RANGE_16_G:
    Serial.println("+-16G");
    break;
  }
  mpu.setGyroRange(MPU6050_RANGE_500_DEG);
  Serial.print("Gyro range set to: ");
  switch (mpu.getGyroRange()) {
  case MPU6050_RANGE_250_DEG:
    Serial.println("+- 250 deg/s");
    break;
  case MPU6050_RANGE_500_DEG:
    Serial.println("+- 500 deg/s");
    break;
  case MPU6050_RANGE_1000_DEG:
    Serial.println("+- 1000 deg/s");
    break;
  case MPU6050_RANGE_2000_DEG:
    Serial.println("+- 2000 deg/s");
    break;
  }


  mpu.setFilterBandwidth(MPU6050_BAND_21_HZ);
  Serial.print("Filter bandwidth set to: ");
  switch (mpu.getFilterBandwidth()) {
  case MPU6050_BAND_260_HZ:
    Serial.println("260 Hz");
    break;
  case MPU6050_BAND_184_HZ:
    Serial.println("184 Hz");
    break;
  case MPU6050_BAND_94_HZ:
    Serial.println("94 Hz");
    break;
  case MPU6050_BAND_44_HZ:
    Serial.println("44 Hz");
    break;
  case MPU6050_BAND_21_HZ:
    Serial.println("21 Hz");
    break;
  case MPU6050_BAND_10_HZ:
    Serial.println("10 Hz");
    break;
  case MPU6050_BAND_5_HZ:
    Serial.println("5 Hz");
    break;
  }


  Serial.println("");
  delay(100);


}


void loop() {
   sensors_event_t a, g, temp;
  mpu.getEvent(&a, &g, &temp);
  if (a.acceleration.x<2 && a.acceleration.y<2 && a.acceleration.z<4){
  Serial.println("It is terrian - A, Go fast");
  digitalWrite(IN1_1, HIGH);  // Enable motor 1 (left wheel 1)
  digitalWrite(IN2_1, LOW);   // Forward direction for motor 1
  digitalWrite(IN3_1, HIGH);  // Forward direction for motor 1


  digitalWrite(IN1_2, HIGH);  // Enable motor 2 (left wheel 2)
  digitalWrite(IN2_2, LOW);   // Forward direction for motor 2
  digitalWrite(IN3_2, HIGH);  // Forward direction for motor 2


  digitalWrite(IN1_3, HIGH);  // Enable motor 3 (right wheel 1)
  digitalWrite(IN2_3, LOW);   // Forward direction for motor 3
  digitalWrite(IN3_3, HIGH);  // Forward direction for motor 3


  digitalWrite(IN1_4, HIGH);  // Enable motor 4 (right wheel 2)
  digitalWrite(IN2_4, LOW);   // Forward direction for motor 4
  digitalWrite(IN3_4, HIGH);  // Forward direction for motor 4


  analogWrite(IN1_1, 255); 
  analogWrite(IN1_2, 255); 
  analogWrite(IN1_3, 255); 
  analogWrite(IN1_4, 255); 
  }
  else{
    Serial.println("It is Terrian -B, Go slow");
    digitalWrite(IN1_1, HIGH);  // Enable motor 1 (left wheel 1)
  digitalWrite(IN2_1, LOW);   // Forward direction for motor 1
  digitalWrite(IN3_1, HIGH);  // Forward direction for motor 1


  digitalWrite(IN1_2, HIGH);  // Enable motor 2 (left wheel 2)
  digitalWrite(IN2_2, LOW);   // Forward direction for motor 2
  digitalWrite(IN3_2, HIGH);  // Forward direction for motor 2


  digitalWrite(IN1_3, HIGH);  // Enable motor 3 (right wheel 1)
  digitalWrite(IN2_3, LOW);   // Forward direction for motor 3
  digitalWrite(IN3_3, HIGH);  // Forward direction for motor 3


  digitalWrite(IN1_4, HIGH);  // Enable motor 4 (right wheel 2)
  digitalWrite(IN2_4, LOW);   // Forward direction for motor 4
  digitalWrite(IN3_4, HIGH);  // Forward direction for motor 4


  analogWrite(IN1_1, 150); 
  analogWrite(IN1_2, 150); 
  analogWrite(IN1_3, 150); 
  analogWrite(IN1_4, 150);
  }
  Serial.print(a.acceleration.x);
  Serial.print('\t');
  Serial.print(a.acceleration.y);
  Serial.print('\t');
  Serial.print(a.acceleration.z);  
  Serial.print('\t');
  Serial.print(g.gyro.x);  
  Serial.print('\t');
  Serial.print(g.gyro.y);
  Serial.print('\t');
  Serial.print(g.gyro.z);
  Serial.println("");
  delay(500);



}
